// Logisim project assignment2.circ as structural Verilog: 2 circuits, main circuit main
module main (
  input  in_1,
  input  in_2,
  input  in_3,
  input  in_4,
  input  in_5,
  input  in_6,
  input  in_7,
  input  in_8,
  output Sum,
  output Carry,
  output Sum_2,
  output Carry_2,
  output Sum_3,
  output Carry_3
);

  wire and_2_out, and_3_out, halfadder_1_out_3, halfadder_1_out_4, halfadder_2_out_4, xor_1_out;

  xor xor_1 (xor_1_out, in_6, in_7);
  xor xor_2 (Sum, in_1, in_2);
  and and_1 (Carry, in_1, in_2);
  xor xor_3 (Sum_3, xor_1_out, in_8);
  and and_2 (and_2_out, in_6, in_7);
  and and_3 (and_3_out, xor_1_out, in_8);
  or or_1 (Carry_3, and_2_out, and_3_out);
  HalfAdder halfadder_1 (.in_1(in_3), .in_2(in_4), .out_3(halfadder_1_out_3), .out_4(halfadder_1_out_4));
  HalfAdder halfadder_2 (.in_1(halfadder_1_out_3), .in_2(in_5), .out_3(Sum_2), .out_4(halfadder_2_out_4));
  or or_2 (Carry_2, halfadder_1_out_4, halfadder_2_out_4);

  // Notes on the sheet:
  //   Full Adder with AND, XOR and OR gates
  //   Half Adder
  //   Full adder with hald adders
endmodule

module HalfAdder (
  input  in_1,
  input  in_2,
  output out_3,
  output out_4
);

  xor xor_1 (out_3, in_1, in_2);
  and and_1 (out_4, in_1, in_2);
endmodule
